// Digital circuit HW9.dig as structural Verilog
module HW9 (
  input  A,
  input  B,
  input  C,
  input  D,
  input  E,
  output Y
);

  wire and_1_out, and_2_out, and_3_out, and_4_out, not_1_out, not_2_out;

  not not_1 (not_1_out, D);
  not not_2 (not_2_out, E);
  and and_1 (and_1_out, not_2_out, not_1_out);
  and and_2 (and_2_out, not_2_out, D);
  and and_3 (and_3_out, E, not_1_out);
  and and_4 (and_4_out, E, D);
  Multiplexer #(.Selector_Bits(3)) multiplexer_1 (
    .sel({A, B, C}), .in_0(not_2_out), .in_1(and_2_out), .in_2(and_3_out), .in_3(and_3_out),
    .in_4(and_1_out), .in_5(and_4_out), .in_6(E), .in_7(D), .out(Y));

  // Notes on the sheet:
  //   (~D)(~E)
  //   (D)(~E)
  //   (~D)(E)
  //   (D)(E)
endmodule
