// Digital circuit 10.5.dig as structural Verilog
module _10_5 (
);

  wire minialu_1_p1;
  wire [2:0] programcounter_1_p2;

  // miniALU minialu_1: pin names not known; wires that end beside it: minialu_1_p1
  // programCounter programcounter_1: pin names not known; wires that end beside it: minialu_1_p1, programcounter_1_p2
  programROM programrom_1 (.A(programcounter_1_p2));  // open: D
endmodule
