// Digital circuit 10.6.dig as structural Verilog
module _10_6 (
  input  [3:0] In_0,
  input  [3:0] In_1,
  input  [3:0] In_2,
  input  [3:0] In_3,
  input  [1:0] N,
  output [3:0] Out
);

  Multiplexer #(.Bits(4), .Selector_Bits(2)) multiplexer_1 (
    .sel(N), .in_0(In_0), .in_1(In_1), .in_2(In_2), .in_3(In_3), .out(Out));
endmodule
