// Digital circuit Lab10_01.dig as structural Verilog
module Lab10_01 (
  input  Input_1,
  input  Inout_2,
  output Output_1
);

  xor xor_1 (Output_1, Input_1, Inout_2);
  LED led_1 (.in(Output_1));
endmodule
