// Digital circuit Lab10_02.dig as structural Verilog
module Lab10_02 (
  input  A,
  input  B,
  input  C_i,
  output S,
  output C_o
);

  fullAdder fulladder_1 (.A(A), .C_i(B), .B(C_i), .S(S), .C_o(C_o));
endmodule

/* Test case:
A B C_{i} S C_{o}
0 0 0     0 0
1 0 0     1 0
0 1 0     1 0
1 1 0     0 1
0 0 1     1 0
1 0 1     0 1
0 1 1     0 1
1 1 1     1 1
*/
