// Digital circuit Lab10_02_1.dig as structural Verilog
module Lab10_02_1 (
  input  [3:0] A,
  input  [3:0] B,
  input  C_i,
  output [3:0] S,
  output C_o
);

  wire fulladder_1_c_o, fulladder_2_c_o, fulladder_3_c_o;

  fullAdder fulladder_1 (.A(A[0]), .C_i(C_i), .B(B[0]), .S(S[0]), .C_o(fulladder_1_c_o));
  fullAdder fulladder_2 (.A(A[1]), .C_i(fulladder_1_c_o), .B(B[1]), .S(S[1]), .C_o(fulladder_2_c_o));
  fullAdder fulladder_3 (.A(A[2]), .C_i(fulladder_2_c_o), .B(B[2]), .S(S[2]), .C_o(fulladder_3_c_o));
  fullAdder fulladder_4 (.A(A[3]), .C_i(fulladder_3_c_o), .B(B[3]), .S(S[3]), .C_o(C_o));
endmodule

/* Test case:
A B C_{i} S C_{o}
0 0 0     0 0
1 0 0     1 0
0 1 0     1 0
1 1 0     0 1
0 0 1     1 0
1 0 1     0 1
0 1 1     0 1
1 1 1     1 1
*/
