// Digital circuit dataRAM.dig as structural Verilog
module dataRAM (
  input  [2:0] in_1,
  input  [3:0] in_2,
  input  in_3,
  input  in_4,
  input  in_5,
  output [3:0] out_6
);

  RAMDualPort #(.AddrBits(3), .Bits(4)) ramdualport_1 (
    .A(in_1), .Din(in_2), .str(in_3), .C(in_4), .ld(in_5), .D(out_6));
endmodule
