// Digital circuit miniALU.dig as structural Verilog
module miniALU (
  input  FlagWrite,
  input  CLK,
  input  [3:0] A,
  input  [3:0] B,
  output F_Zero,
  output [3:0] Sum
);

  wire nor_1_out;

  rcAdder rcadder_1 (.A(A), .B(B), .C_i(1'b0), .S(Sum));  // open: C_o
  nor nor_1 (nor_1_out, Sum[0], Sum[1], Sum[2], Sum[3]);
  Register register_1 (.D(nor_1_out), .C(CLK), .en(FlagWrite), .Q(F_Zero));
endmodule
