// Digital circuit programCounter.dig as structural Verilog
module programCounter (
  input  CLK,
  input  [3:0] in,
  input  ld,
  input  clr,
  output [3:0] out,
  output ovf
);

  CounterPreset #(.Bits(4)) counterpreset_1 (
    .en(1'b1), .C(CLK), .dir(1'b0), .in(in), .ld(ld), .clr(clr), .out(out), .ovf(ovf));
endmodule
