// Digital circuit programROM.dig as structural Verilog
module programROM (
  input  [2:0] A,
  output [7:0] D
);

  ROM #(.AddrBits(3), .Bits(8)) rom_1 (.A(A), .sel(1'b1), .D(D));

  // Notes on the sheet:
  //   contents of rom_1 (hex, n*v repeats v):
  //   0,1,2,3,4,5,6,7
endmodule
