// Digital circuit rcAdder.dig as structural Verilog
module rcAdder (
  input  [3:0] A,
  input  [3:0] B,
  input  C_i,
  output [3:0] S,
  output C_o
);

  wire fulladder_1_c_o, fulladder_2_c_o, fulladder_3_c_o;

  fullAdder fulladder_1 (.A(A[0]), .C_i(C_i), .B(B[0]), .S(S[0]), .C_o(fulladder_1_c_o));
  fullAdder fulladder_2 (.A(A[1]), .C_i(fulladder_1_c_o), .B(B[1]), .S(S[1]), .C_o(fulladder_2_c_o));
  fullAdder fulladder_3 (.A(A[2]), .C_i(fulladder_2_c_o), .B(B[2]), .S(S[2]), .C_o(fulladder_3_c_o));
  fullAdder fulladder_4 (.A(A[3]), .C_i(fulladder_3_c_o), .B(B[3]), .S(S[3]), .C_o(C_o));
endmodule

/* Test case:
A  B  C_{i}  S  C_{o}
0  0  0   0  0
1  1  0   2  0
2  2  0   4  0
3  3  0   6  0
5  5  0  10  0
8  8  0  16  1
9  3  0  12  0
7  1  1   9  0
15 1  0  16  1
*/
