// Digital circuit registerFile.dig as structural Verilog
module registerFile (
  input  we,
  input  [2:0] R_w,
  input  CLK,
  input  [2:0] R_a,
  input  [2:0] R_b,
  input  [3:0] D_in,
  output [3:0] D_a,
  output [3:0] D_b
);

  RegisterFile #(.AddrBits(3), .Bits(4)) registerfile_1 (
    .Din(D_in), .we(we), .Rw(R_w), .C(CLK), .Ra(R_a), .Rb(R_b), .Da(D_a), .Db(D_b));
endmodule
